# Fritzing sketch sensoro001 (saved by Fritzing 0.9.6b)
breadboards: 1

parts:
  NodeMCU = ESP8266 NodeMCU LoLin module
  M1 = IR break beam 3mm rx [package=THT]
  M2 = IR break beam 3mm tx [package=THT]

nets (from the breadboard view):
  N1: NodeMCU.connector4, M1.pin2
  N2: NodeMCU.connector19, M1.pin1, M2.pin1
  N3: NodeMCU.connector33, M1.pin3, M2.pin2

custom parts:
  IR break beam 3mm rx: Infrared break beam Sensor rx module.
  IR break beam 3mm tx: Infrared break beam Sensor tx module.
