# Fritzing sketch sensoro2 (saved by Fritzing 0.9.6b)
breadboards: 1

parts:
  U1 = ESP8266 NodeMCU LoLin module
  C1 = Capacitor [package=cap-pth-small2]
  R1 = Resistor [tolerance=±5% power=0.25 resistance=220 package=THT]
  R2 = Resistor [tolerance=±5% power=0.25 resistance=220 package=THT]

nets:
  N1: U1.D2, R1.Pin_0
  N2: U1.D3, R2.Pin_0
  N3: U1.GND, C1.2
  N4: U1.A0, C1.1, R1.Pin_1, R2.Pin_1

custom parts:
  ESP8266 NodeMCU LoLin module: ESP8266 based NodeMCU
